# Fritzing sketch Schematic (saved by Fritzing 0.9.3b)
breadboards: 1

parts:
  3 = Weather Shield [part_number=DEV-12081]
  1 = Arduino Mega ADK (Rev3)
  2 = Arduino Board Ethernet  # not connected
  U1 = RJ45 Jack [package=rj45-8]  # not connected
  U2 = RJ45 Jack [package=rj45-8]  # not connected
  7 = Gas Sensor Breakout Board
  5 = Gas Sensor Breakout Board
  4 = Gas Sensor Breakout Board
  6 = Gas Sensor Breakout Board
  Power_plug1 = Power plug  # not connected

nets:
  N1: 3.IOREF, 1.IOREF#303
  N2: 1.A8, 6.A1
  N3: 1.A9, 7.A1
  N4: 1.A6, 4.A1
  N5: 1.A7, 5.A1
  N6: 1.D17/RX2, 7.H1
  N7: 1.D16/TX2, 6.H1
  N8: 1.D15/RX3, 5.H1
  N9: 1.D14/TX3, 4.H1
  N10: 7.B1, 6.B1
  GND: 7.GND, 6.GND
  GND_2: 5.GND, 4.GND
  N11: 5.B1, 4.B1

custom parts:
  Weather Shield: Weather Shield includes: - ALS-PT19 Light Sensor - HTU21D Humidity Sensor - MPL3115A2 - TEMT6000 Check out the product page on www.sparkfun.com for documentation!
